// Logisim project 1 D_JK.circ as structural Verilog: 1 circuit, main circuit main
module main (
  input  D,
  input  J,
  input  K,
  output Q_star,
  output Q,
  output Q_2,
  output Q_star_2
);

  wire clock_1_out, clock_2_out, nand_1_out, nand_2_out, nand_3_out, nand_4_out;

  Clock clock_1 (.out(clock_1_out));
  Clock clock_2 (.out(clock_2_out));
  nand nand_1 (nand_1_out, ~D, clock_1_out);  // NAND_Gate
  nand nand_2 (nand_2_out, clock_1_out, D);
  nand nand_3 (nand_3_out, Q_star_2, J, clock_2_out);
  nand nand_4 (nand_4_out, clock_2_out, K, Q_2);
  nand nand_5 (Q_star, nand_1_out, Q);
  nand nand_6 (Q, Q_star, nand_2_out);
  nand nand_7 (Q_2, nand_3_out, Q_star_2);
  nand nand_8 (Q_star_2, Q_2, nand_4_out);
endmodule
