// Logisim project 10 ULA_OK.circ as structural Verilog: 10 circuits, main circuit main
module main (
  input  [7:0] A,
  input  [7:0] B,
  input  [3:0] in_3,
  output [7:0] out_4
);

  wire [7:0] and_1_out, n2direita_1_out, n2esquerda_1_out, nand_1_out, nor_1_out, not_1_out, or_1_out,
       somador_8bits_1_out, sub_8bits_1_out, xor_1_out;

  assign and_1_out = A & B;  // AND_Gate and_1, 8 bits wide
  assign or_1_out = A | B;  // OR_Gate or_1, 8 bits wide
  assign not_1_out = ~A;  // NOT_Gate not_1, 8 bits wide
  assign nor_1_out = ~(A | B);  // NOR_Gate nor_1, 8 bits wide
  assign nand_1_out = ~(A & B);  // NAND_Gate nand_1, 8 bits wide
  assign xor_1_out = A ^ B;  // XOR_Gate xor_1, 8 bits wide
  _2esquerda u_2esquerda_1 (.A(A), .Out(n2esquerda_1_out));
  _2direita u_2direita_1 (.A(A), .Out(n2direita_1_out));
  somador_8bits somador_8bits_1 (.A(A), .B(B), .Cin(1'b0), .Out(somador_8bits_1_out));  // open: out_4
  sub_8bits sub_8bits_1 (.A(A), .B(B), .Bin(1'b0), .Out(sub_8bits_1_out));  // open: out_4
  multiplexador_8_bits multiplexador_8_bits_1 (
    .AND(and_1_out), .OR(or_1_out), .NOT(not_1_out), .NOR(nor_1_out), .NAND(nand_1_out), .XOR(xor_1_out),
    .SHIFT_ESQ(n2esquerda_1_out), .SHIFT_DIR(n2direita_1_out), .SOMA(somador_8bits_1_out),
    .SUB(sub_8bits_1_out), .Cod(in_3), .Out(out_4));

  // Notes on the sheet:
  //   0000 - AND
  //   0001 - OR
  //   0010 - NOT
  //   0011 - NOR
  //   0100 - NAND
  //   0101 - XOR
  //   0110 - Shift 2 Bits Esquerda
  //   0111 - Shift 2 Bits Direita
  //   1000 - Soma
  //   1001 - Subtração
endmodule

module somador_8bits (
  input  Cin,
  input  [7:0] A,
  input  [7:0] B,
  output out_4,
  output [7:0] Out
);

  wire adder_1_cout, adder_2_cout, adder_3_cout, adder_4_cout, adder_5_cout, adder_6_cout, adder_7_cout;

  adder adder_1 (.A(A[0]), .B(B[0]), .Cin(Cin), .Cout(adder_1_cout), .Sum(Out[0]));
  adder adder_2 (.A(A[1]), .B(B[1]), .Cin(adder_1_cout), .Cout(adder_2_cout), .Sum(Out[1]));
  adder adder_3 (.A(A[2]), .B(B[2]), .Cin(adder_2_cout), .Cout(adder_3_cout), .Sum(Out[2]));
  adder adder_4 (.A(A[3]), .B(B[3]), .Cin(adder_3_cout), .Cout(adder_4_cout), .Sum(Out[3]));
  adder adder_5 (.A(A[4]), .B(B[4]), .Cin(adder_4_cout), .Cout(adder_5_cout), .Sum(Out[4]));
  adder adder_6 (.A(A[5]), .B(B[5]), .Cin(adder_5_cout), .Cout(adder_6_cout), .Sum(Out[5]));
  adder adder_7 (.A(A[6]), .B(B[6]), .Cin(adder_6_cout), .Cout(adder_7_cout), .Sum(Out[6]));
  adder adder_8 (.A(A[7]), .B(B[7]), .Cin(adder_7_cout), .Cout(out_4), .Sum(Out[7]));
endmodule

module adder (
  input  A,
  input  B,
  input  Cin,
  output Sum,
  output Cout
);

  wire and_1_out, and_2_out, xor_1_out;

  xor xor_1 (xor_1_out, A, B);
  and and_1 (and_1_out, xor_1_out, Cin);
  and and_2 (and_2_out, A, B);
  xor xor_2 (Sum, xor_1_out, Cin);
  or or_1 (Cout, and_1_out, and_2_out);
endmodule

module meio_sub (
  input  A,
  input  B,
  output Dif,
  output C
);

  wire not_1_out;

  not not_1 (not_1_out, A);
  xor xor_1 (Dif, A, B);
  and and_1 (C, B, not_1_out);
endmodule

module sub (
  input  A,
  input  B,
  input  Bin,
  output Dif,
  output Bout
);

  wire meio_sub_1_c, meio_sub_1_dif, meio_sub_2_c;

  meio_sub meio_sub_1 (.A(A), .B(B), .Dif(meio_sub_1_dif), .C(meio_sub_1_c));
  meio_sub meio_sub_2 (.A(meio_sub_1_dif), .B(Bin), .Dif(Dif), .C(meio_sub_2_c));
  or or_1 (Bout, meio_sub_2_c, meio_sub_1_c);
endmodule

module sub_8bits (
  input  [7:0] A,
  input  [7:0] B,
  input  Bin,
  output out_4,
  output [7:0] Out
);

  wire sub_2_bout, sub_3_bout, sub_4_bout, sub_5_bout, sub_6_bout, sub_7_bout, sub_8_bout;

  sub sub_1 (.A(A[7]), .B(B[7]), .Bin(sub_2_bout), .Dif(Out[7]), .Bout(out_4));
  sub sub_2 (.A(A[6]), .B(B[6]), .Bin(sub_3_bout), .Dif(Out[6]), .Bout(sub_2_bout));
  sub sub_3 (.A(A[5]), .B(B[5]), .Bin(sub_4_bout), .Dif(Out[5]), .Bout(sub_3_bout));
  sub sub_4 (.A(A[4]), .B(B[4]), .Bin(sub_5_bout), .Dif(Out[4]), .Bout(sub_4_bout));
  sub sub_5 (.A(A[3]), .B(B[3]), .Bin(sub_6_bout), .Dif(Out[3]), .Bout(sub_5_bout));
  sub sub_6 (.A(A[2]), .B(B[2]), .Bin(sub_7_bout), .Dif(Out[2]), .Bout(sub_6_bout));
  sub sub_7 (.A(A[1]), .B(B[1]), .Bin(sub_8_bout), .Dif(Out[1]), .Bout(sub_7_bout));
  sub sub_8 (.A(A[0]), .B(B[0]), .Bin(Bin), .Dif(Out[0]), .Bout(sub_8_bout));
endmodule

module _2esquerda (
  input  [7:0] A,
  output [7:0] Out
);


  assign Out = {A[5:0], 2'b00};
endmodule

module _2direita (
  input  [7:0] A,
  output [7:0] Out
);


  assign Out = {2'b00, A[7:2]};
endmodule

module multiplexador_8_bits (
  input  [7:0] AND,
  input  [7:0] OR,
  input  [7:0] NOT,
  input  [7:0] NOR,
  input  [7:0] NAND,
  input  [7:0] XOR,
  input  [7:0] SHIFT_ESQ,
  input  [7:0] SHIFT_DIR,
  input  [7:0] SOMA,
  input  [7:0] SUB,
  input  [3:0] Cod,
  output [7:0] Out
);

  multiplexador_10 multiplexador_10_1 (
    .a(AND[0]), .b(OR[0]), .c(NOT[0]), .d(NOR[0]), .e(NAND[0]), .f(XOR[0]), .g(SHIFT_ESQ[0]),
    .h(SHIFT_DIR[0]), .i(SOMA[0]), .j(SUB[0]), .Cod(Cod), .Out(Out[0]));
  multiplexador_10 multiplexador_10_2 (
    .a(AND[1]), .b(OR[1]), .c(NOT[1]), .d(NOR[1]), .e(NAND[1]), .f(XOR[1]), .g(SHIFT_ESQ[1]),
    .h(SHIFT_DIR[1]), .i(SOMA[1]), .j(SUB[1]), .Cod(Cod), .Out(Out[1]));
  multiplexador_10 multiplexador_10_3 (
    .a(AND[2]), .b(OR[2]), .c(NOT[2]), .d(NOR[2]), .e(NAND[2]), .f(XOR[2]), .g(SHIFT_ESQ[2]),
    .h(SHIFT_DIR[2]), .i(SOMA[2]), .j(SUB[2]), .Cod(Cod), .Out(Out[2]));
  multiplexador_10 multiplexador_10_4 (
    .a(AND[3]), .b(OR[3]), .c(NOT[3]), .d(NOR[3]), .e(NAND[3]), .f(XOR[3]), .g(SHIFT_ESQ[3]),
    .h(SHIFT_DIR[3]), .i(SOMA[3]), .j(SUB[3]), .Cod(Cod), .Out(Out[3]));
  multiplexador_10 multiplexador_10_5 (
    .a(AND[4]), .b(OR[4]), .c(NOT[4]), .d(NOR[4]), .e(NAND[4]), .f(XOR[4]), .g(SHIFT_ESQ[4]),
    .h(SHIFT_DIR[4]), .i(SOMA[4]), .j(SUB[4]), .Cod(Cod), .Out(Out[4]));
  multiplexador_10 multiplexador_10_6 (
    .a(AND[5]), .b(OR[5]), .c(NOT[5]), .d(NOR[5]), .e(NAND[5]), .f(XOR[5]), .g(SHIFT_ESQ[5]),
    .h(SHIFT_DIR[5]), .i(SOMA[5]), .j(SUB[5]), .Cod(Cod), .Out(Out[5]));
  multiplexador_10 multiplexador_10_7 (
    .a(AND[6]), .b(OR[6]), .c(NOT[6]), .d(NOR[6]), .e(NAND[6]), .f(XOR[6]), .g(SHIFT_ESQ[6]),
    .h(SHIFT_DIR[6]), .i(SOMA[6]), .j(SUB[6]), .Cod(Cod), .Out(Out[6]));
  multiplexador_10 multiplexador_10_8 (
    .a(AND[7]), .b(OR[7]), .c(NOT[7]), .d(NOR[7]), .e(NAND[7]), .f(XOR[7]), .g(SHIFT_ESQ[7]),
    .h(SHIFT_DIR[7]), .i(SOMA[7]), .j(SUB[7]), .Cod(Cod), .Out(Out[7]));

  // Notes on the sheet:
  //   0000 - AND
  //   0001 - OR
  //   0010 - NOT
  //   0011 - NOR
  //   0100 - NAND
  //   0101 - XOR
  //   0110 - Shift 2 Bits Esquerda
  //   0111 - Shift 2 Bits Direita
  //   1000 - Soma
  //   1001 - Subtração
endmodule

module multiplexador_10 (
  input  [3:0] Cod,
  input  a,
  input  b,
  input  c,
  input  d,
  input  e,
  input  f,
  input  g,
  input  h,
  input  i,
  input  j,
  output Out
);

  wire and_1_out, and_2_out, and_3_out, and_4_out, and_5_out, and_6_out, and_7_out, and_8_out, and_9_out,
       and_10_out;

  and and_1 (and_1_out, ~Cod[3], ~Cod[2], ~Cod[1], ~Cod[0], a);  // AND_Gate
  and and_2 (and_2_out, ~Cod[3], ~Cod[2], ~Cod[1], Cod[0], b);  // AND_Gate
  and and_3 (and_3_out, ~Cod[3], ~Cod[2], Cod[1], ~Cod[0], c);  // AND_Gate
  and and_4 (and_4_out, ~Cod[3], ~Cod[2], Cod[1], Cod[0], d);  // AND_Gate
  and and_5 (and_5_out, ~Cod[3], Cod[2], ~Cod[1], ~Cod[0], e);  // AND_Gate
  and and_6 (and_6_out, ~Cod[3], Cod[2], ~Cod[1], Cod[0], f);  // AND_Gate
  and and_7 (and_7_out, ~Cod[3], Cod[2], Cod[1], ~Cod[0], g);  // AND_Gate
  and and_8 (and_8_out, ~Cod[3], Cod[2], Cod[1], Cod[0], h);  // AND_Gate
  and and_9 (and_9_out, Cod[3], ~Cod[2], ~Cod[1], ~Cod[0], i);  // AND_Gate
  and and_10 (and_10_out, Cod[3], ~Cod[2], ~Cod[1], Cod[0], j);  // AND_Gate
  or or_1 (Out, and_1_out, and_2_out, and_3_out, and_4_out, and_5_out, and_6_out, and_7_out, and_8_out, and_9_out, and_10_out);

  // Notes on the sheet:
  //   0000 - AND
  //   0001 - OR
  //   0010 - NOT
  //   0011 - NOR
  //   0100 - NAND
  //   0101 - XOR
  //   0111 - Shift 2 Bits Direita
  //   1000 - Soma
  //   1001 - Subtração
  //   0110 - Shift 2 Bits Esquerda
endmodule
