// Logisim project 12 Máquina de Estados.circ as structural Verilog: 1 circuit, main circuit main
module main (
  input  in_1,
  input  in_2,
  input  in_3,
  input  in_4,
  input  in_5,
  input  in_6,
  input  in_7,
  input  in_8,
  input  P,
  output R
);

  wire and_1_out, and_2_out, and_3_out, and_4_out, and_5_out, and_6_out, and_7_out, and_8_out, and_9_out,
       clock_1_out, nand_1_out, nand_2_out, nand_3_out, nand_4_out, nand_5_out, nand_6_out, nand_7_out,
       nand_8_out, nand_9_out, nand_10_out, nand_11_out, nand_12_out, nand_13_out, nand_14_out, nand_15_out,
       nand_16_out, nand_17_out, nand_18_out, nand_19_out, nand_20_out, nand_21_out, nand_22_out,
       nand_23_out, nand_24_out, nand_25_out, nand_26_out, nand_27_out, nand_28_out, nand_29_out,
       nand_30_out, nand_32_out, not_1_out, not_2_out, not_3_out, not_4_out, not_5_out, not_6_out, not_7_out,
       not_8_out, not_9_out, not_10_out, not_11_out, not_12_out, not_13_out, not_14_out, not_15_out,
       not_16_out, not_17_out, not_18_out, not_19_out, not_20_out, not_21_out, not_22_out, not_23_out,
       or_1_out, or_2_out, or_3_out;

  and and_1 (and_1_out, not_5_out, R);
  and and_2 (and_2_out, not_5_out, nand_7_out);
  and and_3 (and_3_out, not_1_out, not_2_out, not_3_out, not_4_out);
  Clock clock_1 (.out(clock_1_out));
  not not_1 (not_1_out, R);
  not not_2 (not_2_out, nand_23_out);
  not not_3 (not_3_out, nand_15_out);
  not not_4 (not_4_out, nand_7_out);
  or or_1 (or_1_out, and_3_out, and_2_out, and_1_out);
  not not_5 (not_5_out, P);
  not not_6 (not_6_out, in_1);
  not not_7 (not_7_out, or_1_out);
  not not_8 (not_8_out, in_5);
  LED A (.in(nand_7_out));
  nand nand_1 (nand_1_out, nand_8_out, or_1_out, clock_1_out);
  nand nand_2 (nand_2_out, not_6_out, nand_1_out, nand_4_out);
  not not_9 (not_9_out, clock_1_out);
  nand nand_3 (nand_3_out, clock_1_out, not_7_out, nand_7_out);
  nand nand_4 (nand_4_out, nand_2_out, nand_3_out, not_8_out);
  LED C (.in(nand_23_out));
  LED D (.in(R));
  LED B (.in(nand_15_out));
  nand nand_5 (nand_5_out, nand_2_out, not_8_out, not_9_out);
  nand nand_6 (nand_6_out, not_9_out, not_6_out, nand_4_out);
  nand nand_7 (nand_7_out, not_6_out, nand_5_out, nand_8_out);
  nand nand_8 (nand_8_out, nand_7_out, nand_6_out, not_8_out);
  and and_4 (and_4_out, P, nand_7_out);
  and and_5 (and_5_out, P, R);
  and and_6 (and_6_out, not_11_out, nand_15_out);
  or or_2 (or_2_out, and_4_out, and_5_out, and_6_out);
  not not_10 (not_10_out, or_2_out);
  not not_11 (not_11_out, P);
  not not_12 (not_12_out, in_2);
  nand nand_9 (nand_9_out, nand_16_out, or_2_out, clock_1_out);
  nand nand_10 (nand_10_out, clock_1_out, not_10_out, nand_15_out);
  not not_13 (not_13_out, in_6);
  nand nand_11 (nand_11_out, not_12_out, nand_9_out, nand_12_out);
  not not_14 (not_14_out, clock_1_out);
  nand nand_12 (nand_12_out, nand_11_out, nand_10_out, not_13_out);
  nand nand_13 (nand_13_out, nand_11_out, not_13_out, not_14_out);
  nand nand_14 (nand_14_out, not_14_out, not_12_out, nand_12_out);
  nand nand_15 (nand_15_out, not_12_out, nand_13_out, nand_16_out);
  nand nand_16 (nand_16_out, nand_15_out, nand_14_out, not_13_out);
  and and_7 (and_7_out, P, nand_15_out);
  or or_3 (or_3_out, and_7_out, and_8_out);
  not not_15 (not_15_out, P);
  and and_8 (and_8_out, not_15_out, nand_23_out);
  not not_16 (not_16_out, or_3_out);
  not not_17 (not_17_out, in_3);
  nand nand_17 (nand_17_out, nand_24_out, or_3_out, clock_1_out);
  nand nand_18 (nand_18_out, clock_1_out, not_16_out, nand_23_out);
  not not_18 (not_18_out, in_7);
  nand nand_19 (nand_19_out, not_17_out, nand_17_out, nand_20_out);
  not not_19 (not_19_out, clock_1_out);
  nand nand_20 (nand_20_out, nand_19_out, nand_18_out, not_18_out);
  nand nand_21 (nand_21_out, nand_19_out, not_18_out, not_19_out);
  nand nand_22 (nand_22_out, not_19_out, not_17_out, nand_20_out);
  nand nand_23 (nand_23_out, not_17_out, nand_21_out, nand_24_out);
  nand nand_24 (nand_24_out, nand_23_out, nand_22_out, not_18_out);
  and and_9 (and_9_out, P, nand_23_out);
  not not_20 (not_20_out, and_9_out);
  not not_21 (not_21_out, in_4);
  nand nand_25 (nand_25_out, nand_32_out, and_9_out, clock_1_out);
  not not_22 (not_22_out, clock_1_out);
  nand nand_26 (nand_26_out, clock_1_out, not_20_out, R);
  not not_23 (not_23_out, in_8);
  nand nand_27 (nand_27_out, not_21_out, nand_25_out, nand_28_out);
  nand nand_28 (nand_28_out, nand_27_out, nand_26_out, not_23_out);
  nand nand_29 (nand_29_out, nand_27_out, not_23_out, not_22_out);
  nand nand_30 (nand_30_out, not_22_out, not_21_out, nand_28_out);
  nand nand_31 (R, not_21_out, nand_29_out, nand_32_out);
  nand nand_32 (nand_32_out, R, nand_30_out, not_23_out);

  // Notes on the sheet:
  //   A
  //   B
  //   C
  //   D
endmodule
