// Logisim project 13 Contador Sincrono.circ as structural Verilog: 1 circuit, main circuit main
module main (
  input  in_1,
  input  in_2,
  input  in_3,
  input  in_4,
  input  in_5,
  input  in_6,
  input  in_7,
  input  in_8,
  output out_9,
  output out_10,
  output out_11,
  output out_12
);

  wire and_1_out, and_2_out, clock_1_out, nand_1_out, nand_2_out, nand_3_out, nand_4_out, nand_5_out,
       nand_6_out, nand_8_out, nand_9_out, nand_10_out, nand_11_out, nand_12_out, nand_13_out, nand_14_out,
       nand_16_out, nand_17_out, nand_18_out, nand_19_out, nand_20_out, nand_21_out, nand_22_out,
       nand_24_out, nand_25_out, nand_26_out, nand_27_out, nand_28_out, nand_29_out, nand_30_out,
       nand_32_out, not_1_out, not_2_out, not_3_out, not_4_out, not_5_out, not_6_out, not_7_out, not_8_out,
       not_9_out, not_10_out, not_11_out, not_12_out, not_13_out, not_14_out, not_15_out, not_16_out;

  Clock clock_1 (.out(clock_1_out));
  and and_1 (and_1_out, and_2_out, out_10);
  not not_1 (not_1_out, clock_1_out);
  not not_2 (not_2_out, in_1);
  nand nand_1 (nand_1_out, nand_8_out, and_1_out, not_1_out);
  nand nand_2 (nand_2_out, not_1_out, and_1_out, out_9);
  not not_3 (not_3_out, in_5);
  nand nand_3 (nand_3_out, not_2_out, nand_1_out, nand_4_out);
  not not_4 (not_4_out, not_1_out);
  nand nand_4 (nand_4_out, nand_3_out, nand_2_out, not_3_out);
  nand nand_5 (nand_5_out, nand_3_out, not_3_out, not_4_out);
  nand nand_6 (nand_6_out, not_4_out, not_2_out, nand_4_out);
  nand nand_7 (out_9, not_2_out, nand_5_out, nand_8_out);
  nand nand_8 (nand_8_out, out_9, nand_6_out, not_3_out);
  not not_5 (not_5_out, clock_1_out);
  not not_6 (not_6_out, in_2);
  nand nand_9 (nand_9_out, nand_16_out, and_2_out, not_5_out);
  nand nand_10 (nand_10_out, not_5_out, and_2_out, out_10);
  not not_7 (not_7_out, in_6);
  nand nand_11 (nand_11_out, not_6_out, nand_9_out, nand_12_out);
  not not_8 (not_8_out, not_5_out);
  nand nand_12 (nand_12_out, nand_11_out, nand_10_out, not_7_out);
  nand nand_13 (nand_13_out, nand_11_out, not_7_out, not_8_out);
  nand nand_14 (nand_14_out, not_8_out, not_6_out, nand_12_out);
  nand nand_15 (out_10, not_6_out, nand_13_out, nand_16_out);
  nand nand_16 (nand_16_out, out_10, nand_14_out, not_7_out);
  and and_2 (and_2_out, out_12, out_11);
  not not_9 (not_9_out, clock_1_out);
  not not_10 (not_10_out, in_3);
  nand nand_17 (nand_17_out, nand_24_out, out_12, not_9_out);
  nand nand_18 (nand_18_out, not_9_out, out_12, out_11);
  not not_11 (not_11_out, in_7);
  nand nand_19 (nand_19_out, not_10_out, nand_17_out, nand_20_out);
  not not_12 (not_12_out, not_9_out);
  nand nand_20 (nand_20_out, nand_19_out, nand_18_out, not_11_out);
  nand nand_21 (nand_21_out, nand_19_out, not_11_out, not_12_out);
  nand nand_22 (nand_22_out, not_12_out, not_10_out, nand_20_out);
  nand nand_23 (out_11, not_10_out, nand_21_out, nand_24_out);
  nand nand_24 (nand_24_out, out_11, nand_22_out, not_11_out);
  not not_13 (not_13_out, clock_1_out);
  not not_14 (not_14_out, in_4);
  nand nand_25 (nand_25_out, nand_32_out, 1'b1, not_13_out);
  nand nand_26 (nand_26_out, not_13_out, 1'b1, out_12);
  not not_15 (not_15_out, in_8);
  nand nand_27 (nand_27_out, not_14_out, nand_25_out, nand_28_out);
  not not_16 (not_16_out, not_13_out);
  nand nand_28 (nand_28_out, nand_27_out, nand_26_out, not_15_out);
  nand nand_29 (nand_29_out, nand_27_out, not_15_out, not_16_out);
  nand nand_30 (nand_30_out, not_16_out, not_14_out, nand_28_out);
  nand nand_31 (out_12, not_14_out, nand_29_out, nand_32_out);
  nand nand_32 (nand_32_out, out_12, nand_30_out, not_15_out);
endmodule
