// Logisim project 17 ContPrimo.circ as structural Verilog: 1 circuit, main circuit Detector Primo
module Detector_Primo (
  input  in_1,
  input  in_2,
  input  in_3,
  input  in_4,
  output out_5
);

  wire and_1_out, and_2_out, and_3_out, xor_1_out;

  and and_1 (and_1_out, in_1, ~in_4);  // AND_Gate
  and and_2 (and_2_out, in_2, ~in_4, ~in_3);  // AND_Gate
  xor xor_1 (xor_1_out, in_3, in_2);
  and and_3 (and_3_out, in_1, xor_1_out);
  or or_1 (out_5, and_1_out, and_3_out, and_2_out);
endmodule
