// Logisim project 2 Multiplexador de 4 entradas.circ as structural Verilog: 1 circuit, main circuit Multiplexador
module Multiplexador (
  input  in_1,
  input  in_2,
  input  a,
  input  b,
  input  c,
  input  d,
  output out_7
);

  wire Ambas_Abertas_out, Ambas_Negadas_out, Chave_A_Negada_out, Chave_B_Negada_out, not_1_out, not_2_out,
       not_3_out, not_4_out;

  not not_1 (not_1_out, in_1);
  not not_2 (not_2_out, in_2);
  not not_3 (not_3_out, in_1);
  not not_4 (not_4_out, in_2);
  and Ambas_Negadas (Ambas_Negadas_out, not_1_out, not_2_out, a);
  and Chave_A_Negada (Chave_A_Negada_out, not_3_out, in_2, b);
  and Chave_B_Negada (Chave_B_Negada_out, in_1, not_4_out, c);
  and Ambas_Abertas (Ambas_Abertas_out, in_1, in_2, d);
  or or_1 (out_7, Ambas_Negadas_out, Chave_A_Negada_out, Chave_B_Negada_out, Ambas_Abertas_out);
endmodule
