// Logisim project 4 Somador de 8 bits com mais 4.circ as structural Verilog: 2 circuits, main circuit main
module main (
  input  in_1,
  input  in_2,
  input  _0,
  input  in_4,
  input  _1,
  input  in_6,
  input  _2,
  input  in_8,
  input  _3,
  input  in_10,
  input  _4,
  input  in_12,
  input  _5,
  input  in_14,
  input  _6,
  input  in_16,
  input  _7,
  input  in_18,
  output out_19,
  output out_20,
  output out_21,
  output out_22,
  output out_23,
  output out_24,
  output out_25,
  output out_26,
  output out_27,
  output out_28
);

  wire somador_1_cout, somador_1_sum, somador_2_cout, somador_2_sum, somador_3_cout, somador_3_sum,
       somador_4_cout, somador_4_sum, somador_5_cout, somador_5_sum, somador_6_cout, somador_6_sum,
       somador_7_cout, somador_7_sum, somador_8_sum, somador_9_cout, somador_10_cout, somador_11_cout,
       somador_12_cout, somador_13_cout, somador_14_cout, somador_15_cout;

  somador somador_1 (.A(_0), .B(in_4), .Cin(in_1), .Cout(somador_1_cout), .Sum(somador_1_sum));
  somador somador_2 (.A(_1), .B(in_6), .Cin(somador_1_cout), .Cout(somador_2_cout), .Sum(somador_2_sum));
  somador somador_3 (.A(_2), .B(in_8), .Cin(somador_2_cout), .Cout(somador_3_cout), .Sum(somador_3_sum));
  somador somador_4 (.A(_3), .B(in_10), .Cin(somador_3_cout), .Cout(somador_4_cout), .Sum(somador_4_sum));
  somador somador_5 (.A(_4), .B(in_12), .Cin(somador_4_cout), .Cout(somador_5_cout), .Sum(somador_5_sum));
  somador somador_6 (.A(_5), .B(in_14), .Cin(somador_5_cout), .Cout(somador_6_cout), .Sum(somador_6_sum));
  somador somador_7 (.A(_6), .B(in_16), .Cin(somador_6_cout), .Cout(somador_7_cout), .Sum(somador_7_sum));
  somador somador_8 (.A(_7), .B(in_18), .Cin(somador_7_cout), .Cout(out_19), .Sum(somador_8_sum));
  somador somador_9 (.A(somador_1_sum), .B(1'b0), .Cin(in_2), .Cout(somador_9_cout), .Sum(out_21));
  somador somador_10 (.A(somador_2_sum), .B(1'b0), .Cin(somador_9_cout), .Cout(somador_10_cout), .Sum(out_22));
  somador somador_11 (.A(somador_3_sum), .B(1'b1), .Cin(somador_10_cout), .Cout(somador_11_cout), .Sum(out_23));
  somador somador_12 (.A(somador_4_sum), .B(1'b0), .Cin(somador_11_cout), .Cout(somador_12_cout), .Sum(out_24));
  somador somador_13 (.A(somador_5_sum), .B(1'b0), .Cin(somador_12_cout), .Cout(somador_13_cout), .Sum(out_25));
  somador somador_14 (.A(somador_6_sum), .B(1'b0), .Cin(somador_13_cout), .Cout(somador_14_cout), .Sum(out_26));
  somador somador_15 (.A(somador_7_sum), .B(1'b0), .Cin(somador_14_cout), .Cout(somador_15_cout), .Sum(out_27));
  somador somador_16 (.A(somador_8_sum), .B(1'b0), .Cin(somador_15_cout), .Cout(out_20), .Sum(out_28));
endmodule

module somador (
  input  A,
  input  B,
  input  Cin,
  output Sum,
  output Cout
);

  wire and_1_out, and_2_out, xor_1_out;

  xor xor_1 (xor_1_out, A, B);
  and and_1 (and_1_out, xor_1_out, Cin);
  and and_2 (and_2_out, A, B);
  xor xor_2 (Sum, xor_1_out, Cin);
  or or_1 (Cout, and_1_out, and_2_out);
endmodule
