// Logisim project 5 Memoria ROM.circ as structural Verilog: 4 circuits, main circuit main
module main (
  input  [7:0] Entrada,
  output [7:0] \Saída 
);

  ROM_x8x4 rom_x8x4_1 (.in_1(Entrada), .out_2(\Saída ));
endmodule

module celula_ROM (
  input  [2:0] Select,
  output [7:0] out
);

  multiplexador_8_bits multiplexador_8_bits_1 (
    .AND(8'h1), .OR(8'h2), .NOT(8'h4), .NOR(8'h8), .NAND(8'h10), .XOR(8'h20), .SHIFT_ESQ(8'h40),
    .SHIFT_DIR(8'h80), .SOMA({8{1'b0}}), .SUB({8{1'b0}}), .Cod({1'b0, Select}), .Out(out));
endmodule

module ROM_x8 (
  input  [5:0] Select,
  output [7:0] out_2
);

  wire [7:0] celula_rom_1_out, celula_rom_2_out, celula_rom_3_out, celula_rom_4_out, celula_rom_5_out,
       celula_rom_6_out, celula_rom_7_out, celula_rom_8_out;

  celula_ROM celula_rom_1 (.Select(Select[2:0]), .out(celula_rom_1_out));
  celula_ROM celula_rom_2 (.Select(Select[2:0]), .out(celula_rom_2_out));
  celula_ROM celula_rom_3 (.Select(Select[2:0]), .out(celula_rom_3_out));
  celula_ROM celula_rom_4 (.Select(Select[2:0]), .out(celula_rom_4_out));
  celula_ROM celula_rom_5 (.Select(Select[2:0]), .out(celula_rom_5_out));
  celula_ROM celula_rom_6 (.Select(Select[2:0]), .out(celula_rom_6_out));
  celula_ROM celula_rom_7 (.Select(Select[2:0]), .out(celula_rom_7_out));
  celula_ROM celula_rom_8 (.Select(Select[2:0]), .out(celula_rom_8_out));
  multiplexador_8_bits multiplexador_8_bits_1 (
    .AND(celula_rom_1_out), .OR(celula_rom_2_out), .NOT(celula_rom_3_out), .NOR(celula_rom_4_out),
    .NAND(celula_rom_5_out), .XOR(celula_rom_6_out), .SHIFT_ESQ(celula_rom_7_out),
    .SHIFT_DIR(celula_rom_8_out), .SOMA({8{1'b0}}), .SUB({8{1'b0}}),
    .Cod({1'b0, Select[3], Select[4], Select[5]}), .Out(out_2));
endmodule

module ROM_x8x4 (
  input  [7:0] in_1,
  output [7:0] out_2
);

  wire [7:0] rom_x8_1_out_2, rom_x8_2_out_2, rom_x8_3_out_2, rom_x8_4_out_2;

  ROM_x8 rom_x8_1 (.Select(in_1[5:0]), .out_2(rom_x8_1_out_2));
  ROM_x8 rom_x8_2 (.Select(in_1[5:0]), .out_2(rom_x8_2_out_2));
  ROM_x8 rom_x8_3 (.Select(in_1[5:0]), .out_2(rom_x8_3_out_2));
  ROM_x8 rom_x8_4 (.Select(in_1[5:0]), .out_2(rom_x8_4_out_2));
  multiplexador_8_bits multiplexador_8_bits_1 (
    .AND(rom_x8_1_out_2), .OR(rom_x8_2_out_2), .NOT(rom_x8_3_out_2), .NOR(rom_x8_4_out_2), .NAND({8{1'b0}}),
    .XOR({8{1'b0}}), .SHIFT_ESQ({8{1'b0}}), .SHIFT_DIR({8{1'b0}}), .SOMA({8{1'b0}}), .SUB({8{1'b0}}),
    .Cod({2'b00, in_1[6], in_1[7]}), .Out(out_2));
endmodule
