// Logisim project 6 RAM.circ as structural Verilog: 7 circuits, main circuit RAM 1x2
module RAM_1x2 (
  input  [1:0] In,
  input  Clock,
  input  On,
  output [1:0] Out
);

  wire and_1_out, d_1_q, d_2_q;

  and and_1 (and_1_out, Clock, On);
  D d_1 (.Clock(and_1_out), .D(In[0]), .Q(d_1_q));  // open: Q_star
  D d_2 (.Clock(and_1_out), .D(In[1]), .Q(d_2_q));  // open: Q_star
  and and_2 (Out[0], On, d_1_q);
  and and_3 (Out[1], On, d_2_q);
endmodule

module RAM_1x4 (
  input  Clock,
  input  [3:0] Entrada,
  input  Ligar,
  input  Limpar,
  output [3:0] \Saída 
);

  RAM_1x2 ram_1x2_1 ();  // open: Clock, In, On, Out
  RAM_1x2 ram_1x2_2 (.Clock(Clock), .In(Entrada[1:0]), .On(Ligar), .Out(\Saída [1:0]));
  RAM_1x2 ram_1x2_3 (.Clock(Clock), .In(Entrada[3:2]), .On(Ligar), .Out(\Saída [3:2]));
endmodule

module RAM_1x8 (
  input  Clock,
  input  [3:0] Entrada,
  input  [1:0] Seletor,
  input  Limpar,
  output [3:0] \Saída 
);

  wire chave_1_o0, chave_1_o1, chave_1_o2, chave_1_o3;
  wire [3:0] \ram_1x4_1_saída , \ram_1x4_2_saída , \ram_1x4_3_saída , \ram_1x4_4_saída ;

  Chave chave_1 (.in_1(Seletor), .O0(chave_1_o0), .O1(chave_1_o1), .O2(chave_1_o2), .O3(chave_1_o3));
  RAM_1x4 ram_1x4_1 (
    .Entrada(Entrada), .Clock(Clock), .Ligar(chave_1_o0), .Limpar(Limpar), .\Saída (\ram_1x4_1_saída ));
  RAM_1x4 ram_1x4_2 (
    .Entrada(Entrada), .Clock(Clock), .Ligar(chave_1_o3), .Limpar(Limpar), .\Saída (\ram_1x4_2_saída ));
  RAM_1x4 ram_1x4_3 (
    .Entrada(Entrada), .Clock(Clock), .Ligar(chave_1_o1), .Limpar(Limpar), .\Saída (\ram_1x4_3_saída ));
  RAM_1x4 ram_1x4_4 (
    .Entrada(Entrada), .Clock(Clock), .Ligar(chave_1_o2), .Limpar(Limpar), .\Saída (\ram_1x4_4_saída ));
  assign \Saída  = \ram_1x4_1_saída  | \ram_1x4_3_saída  | \ram_1x4_2_saída  | \ram_1x4_4_saída ;  // OR_Gate or_1, 4 bits wide
endmodule

module Chave (
  input  [1:0] in_1,
  output O0,
  output O1,
  output O2,
  output O3
);

  and and_1 (O0, ~in_1[0], ~in_1[1]);  // AND_Gate
  and and_2 (O1, ~in_1[0], in_1[1]);  // AND_Gate
  and and_3 (O2, in_1[0], ~in_1[1]);  // AND_Gate
  and and_4 (O3, in_1[0], in_1[1]);
endmodule

// Limpar
module RAM_Comp (
  input  Clock,
  input  [7:0] In,
  input  [1:0] Seletor,
  output [7:0] Out
);

  RAM_8bits ram_8bits_1 (.Entrada(In), .Seletor(Seletor), .in_1(Clock), .Out(Out));
endmodule

module D (
  input  Clock,
  input  D,
  output Q_star,
  output Q
);

  wire nand_1_out, nand_2_out;

  nand nand_1 (nand_1_out, ~D, Clock);  // NAND_Gate
  nand nand_2 (nand_2_out, Clock, D);
  nand nand_3 (Q_star, nand_1_out, Q);
  nand nand_4 (Q, Q_star, nand_2_out);

  // Notes on the sheet:
  //   D
  //   Q*
  //   Q
endmodule

module RAM_8bits (
  input  in_1,
  input  [7:0] Entrada,
  input  [1:0] Seletor,
  output [7:0] Out
);

  RAM_1x8 ram_1x8_1 (.Entrada(Entrada[3:0]), .Seletor(Seletor), .Clock(in_1), .\Saída (Out[3:0]));  // open: Limpar
  RAM_1x8 ram_1x8_2 (.Entrada(Entrada[7:4]), .Seletor(Seletor), .Clock(in_1), .\Saída (Out[7:4]));  // open: Limpar
endmodule
