// Logisim project 7 Banco de Registradores de 8 bits.circ as structural Verilog: 3 circuits, main circuit Registrador
module Registrador (
  input  in_1,
  input  Clock,
  input  [7:0] In,
  output [7:0] Out
);

  D d_1 (.in_1(Clock), .D(In[7]), .Q(Out[7]));  // open: Q_star
  D d_2 (.in_1(Clock), .D(In[6]), .Q(Out[6]));  // open: Q_star
  D d_3 (.in_1(Clock), .D(In[5]), .Q(Out[5]));  // open: Q_star
  D d_4 (.in_1(Clock), .D(In[4]), .Q(Out[4]));  // open: Q_star
  D d_5 (.in_1(Clock), .D(In[3]), .Q(Out[3]));  // open: Q_star
  D d_6 (.in_1(Clock), .D(In[2]), .Q(Out[2]));  // open: Q_star
  D d_7 (.in_1(Clock), .D(In[1]), .Q(Out[1]));  // open: Q_star
  D d_8 (.in_1(Clock), .D(In[0]), .Q(Out[0]));  // open: Q_star
endmodule

module Banco (
  input  in_1,
  input  [1:0] \Seleção ,
  input  [1:0] \Seleção_2 ,
  input  [7:0] In_D,
  input  in_5,
  output [7:0] out_6
);

  wire buffer_1_out, clock_1_out, demultiplexer_1_out0, demultiplexer_1_out1, demultiplexer_1_out2,
       demultiplexer_1_out3;
  wire [7:0] registrador_1_out, registrador_2_out, registrador_3_out, registrador_4_out;

  buf buffer_1 (buffer_1_out, clock_1_out);
  Clock clock_1 (.out(clock_1_out));
  Demultiplexer #(.select(2), .enable("false")) demultiplexer_1 (
    .out0(demultiplexer_1_out0), .out1(demultiplexer_1_out1), .out2(demultiplexer_1_out2),
    .out3(demultiplexer_1_out3), .in(buffer_1_out), .sel(\Seleção ));
  Registrador registrador_1 (.in_1(in_5), .Clock(demultiplexer_1_out0), .In(In_D), .Out(registrador_1_out));
  Registrador registrador_2 (.in_1(in_5), .Clock(demultiplexer_1_out1), .In(In_D), .Out(registrador_2_out));
  Multiplexer #(.select(2), .width(8), .enable("false")) multiplexer_1 (
    .in0(registrador_1_out), .in1(registrador_2_out), .in2(registrador_3_out), .in3(registrador_4_out),
    .out(out_6), .sel(\Seleção_2 ));
  Registrador registrador_3 (.in_1(in_5), .Clock(demultiplexer_1_out2), .In(In_D), .Out(registrador_3_out));
  Registrador registrador_4 (.in_1(in_5), .Clock(demultiplexer_1_out3), .In(In_D), .Out(registrador_4_out));
endmodule

module D (
  input  in_1,
  input  D,
  output Q_star,
  output Q
);

  wire nand_1_out, nand_2_out;

  nand nand_1 (nand_1_out, ~D, in_1);  // NAND_Gate
  nand nand_2 (nand_2_out, in_1, D);
  nand nand_3 (Q_star, nand_1_out, Q);
  nand nand_4 (Q, Q_star, nand_2_out);
endmodule
