// Logisim project 9 Detector de Sequência Binário.circ as structural Verilog: 2 circuits, main circuit main
module main (
  input  [7:0] In,
  output out_2
);

  wire and_1_out, and_2_out, and_3_out, and_4_out, and_5_out, and_6_out;

  and and_1 (and_1_out, In[0], ~In[1], In[2]);  // AND_Gate
  and and_2 (and_2_out, In[1], ~In[2], In[3]);  // AND_Gate
  and and_3 (and_3_out, In[2], ~In[3], In[4]);  // AND_Gate
  and and_4 (and_4_out, In[3], ~In[4], In[5]);  // AND_Gate
  and and_5 (and_5_out, In[4], ~In[5], In[6]);  // AND_Gate
  and and_6 (and_6_out, In[5], ~In[6], In[7]);  // AND_Gate
  or or_1 (out_2, and_1_out, and_2_out, and_3_out, and_4_out, and_5_out, and_6_out);
endmodule

module flip_d (
  input  Clock,
  input  D,
  output Q,
  output Q_star
);

  wire nand_1_out, nand_2_out;

  nand nand_1 (nand_1_out, ~D, Clock);  // NAND_Gate
  nand nand_2 (nand_2_out, Clock, D);
  nand nand_3 (Q_star, nand_1_out, Q);
  nand nand_4 (Q, Q_star, nand_2_out);

  // Notes on the sheet:
  //   D
  //   Q*
  //   Q
endmodule
