// Logisim project Extensor de Sinal.circ as structural Verilog: 1 circuit, main circuit main
module main (
  input  [7:0] INPUTS,
  input  \Tipo_de_Extensão ,
  output [15:0] Sinal_Final
);


  assign Sinal_Final = {{8{\Tipo_de_Extensão }}, INPUTS};
endmodule
