// Logisim project Somador.circ as structural Verilog: 2 circuits, main circuit main
module main (
  input  in_1,
  input  _0,
  input  in_3,
  input  _1,
  input  in_5,
  input  _2,
  input  in_7,
  input  _3,
  input  in_9,
  input  _4,
  input  in_11,
  input  _5,
  input  in_13,
  input  _6,
  input  in_15,
  input  _7,
  input  in_17,
  output out_18,
  output out_19,
  output out_20,
  output out_21,
  output out_22,
  output out_23,
  output out_24,
  output out_25,
  output out_26
);

  wire somador_1_cout, somador_2_cout, somador_3_cout, somador_4_cout, somador_5_cout, somador_6_cout,
       somador_7_cout;

  somador somador_1 (.A(_0), .B(in_3), .Cin(in_1), .Cout(somador_1_cout), .Sum(out_19));
  somador somador_2 (.A(_1), .B(in_5), .Cin(somador_1_cout), .Cout(somador_2_cout), .Sum(out_20));
  somador somador_3 (.A(_2), .B(in_7), .Cin(somador_2_cout), .Cout(somador_3_cout), .Sum(out_21));
  somador somador_4 (.A(_3), .B(in_9), .Cin(somador_3_cout), .Cout(somador_4_cout), .Sum(out_22));
  somador somador_5 (.A(_4), .B(in_11), .Cin(somador_4_cout), .Cout(somador_5_cout), .Sum(out_23));
  somador somador_6 (.A(_5), .B(in_13), .Cin(somador_5_cout), .Cout(somador_6_cout), .Sum(out_24));
  somador somador_7 (.A(_6), .B(in_15), .Cin(somador_6_cout), .Cout(somador_7_cout), .Sum(out_25));
  somador somador_8 (.A(_7), .B(in_17), .Cin(somador_7_cout), .Cout(out_18), .Sum(out_26));
endmodule

module somador (
  input  A,
  input  B,
  input  Cin,
  output Sum,
  output Cout
);

  wire and_1_out, and_2_out, xor_1_out;

  xor xor_1 (xor_1_out, A, B);
  and and_1 (and_1_out, xor_1_out, Cin);
  and and_2 (and_2_out, A, B);
  xor xor_2 (Sum, xor_1_out, Cin);
  or or_1 (Cout, and_1_out, and_2_out);
endmodule
